# Fritzing sketch gesture vocalizer (saved by Fritzing 0.9.3b)
breadboards: 1

parts:
  Part1 = Arduino Uno (Rev3) - ICSP
  Part2 = Bluetooth HC-05 Macho
  R1 = Basic Flex Resistor
  R2 = Basic Flex Resistor
  R3 = Basic Flex Resistor
  R4 = Basic Flex Resistor
  Part3 = InvenSense MPU6050
  R5 = Resistor [tolerance=±5% resistance=220 package="0402 [SMD]"]
  R6 = Resistor [tolerance=±5% resistance=220 package="0402 [SMD]"]  # not connected
  R7 = Resistor [tolerance=±5% resistance=220 package="0402 [SMD]"]  # not connected
  R8 = Resistor [tolerance=±5% resistance=220 package="0402 [SMD]"]

nets:
  N1: Part1.A0, R2.Pin_2, R5.Pin_0
  N2: Part1.A1, R3.Pin_2
  N3: Part1.A2, R4.Pin_2
  N4: Part1.A3, R1.Pin_2, R8.Pin_0
  N5: Part1.A4/SDA, Part3.SDA
  N6: Part1.A5/SCL, Part3.SCL
  N7: Part1.D1/TX, Part2.RXD
  VCC: Part2.VCC, R1.pin_1, Part3.VCC
  GND: Part2.GND, Part3.GND, R8.Pin_1
